# Fritzing sketch button_toggle_led_diagram (saved by Fritzing 0.9.3b)
breadboards: 1

parts:
  Part1 = Arduino Uno (Rev3)
  R1 = Resistor [tolerance=±5% resistance=330 package=THT]
  S1 = Pushbutton [package="[THT]"]
  LED1 = LED - 5mm [color="Red (633nm)" package="5 mm [THT]"]

nets:
  N1: Part1.D3_PWM, R1.Pin_0
  N2: Part1.D7, S1.Pin_3, S1.Pin_4
  N3: Part1.GND, S1.Pin_1, S1.Pin_2, LED1.cathode
  N4: R1.Pin_1, LED1.anode
